# Fritzing sketch mqtt-ds18b20 (saved by Fritzing 0.9.1b)
circuit board: 4.99658cm x 4cm
breadboards: 1

parts:
  U1 = ESP8266 WiFi Module [part_number=ESP8266]
  R1 = Resistor [tolerance=±5% resistance=4.7k package=THT]
  C1 = Capacitor Polarized [package=cpol-radial-100uf-25v]
  T1 = LM35 Temperature Sensor [package="TO92 [THT]"]
  RHT1 = Humidity and Temperature Sensor RHT03
  R2 = Resistor [tolerance=±5% resistance=220 package=THT]
  J1 = Screw terminal - 2 pins [package=THT]
  J2 = Screw terminal - 2 pins [package=THT]
  S1 = Momentary Switch [package=tactile-pth]
  JP4 = Header 1 [package=1x01_offset]
  JP5 = Header 1 [package=1x01_offset]
  JP7 = Header 1 [package=1x01_offset]
  JP6 = Header 1 [package=1x01_offset]
  IC1 = Voltage Regulator LM1117 [package=sot223]
  Pad1 = Pad [width=6.0630880831705 height=5.34174604878208 connect=center]  # not connected

nets:
  N1: U1.RXD, JP4.1
  VCC: U1.VCC, U1.CH_PD, R1.Pin_1, C1.+, RHT1.Vcc, R2.Pin_0, JP7.1, IC1.OUT
  N2: U1.GPIO_0, RHT1.Data-signal, R2.Pin_1, S1.1
  N3: U1.GPIO_2, R1.Pin_0, T1.Vout, J2.pin2
  GND: U1.GND, C1.-, T1.GND, RHT1.GND_2, J1.pin2, J2.pin1, S1.4, JP6.1, IC1.ADJ
  N4: U1.TXD, JP5.1
  N5: J1.pin1, IC1.IN

notes:
  GND
  VCC
  (3.3v)
  (4-7v)
  1wire
  data
  DHT11/22
  ds18b20
  4.7K
  1K
  HuelvaYork 2015-04
  RX
  TX
  Gnd

custom parts:
  ESP8266 WiFi Module: Generic WiFi Module based on the ESP8266 with onboard PCB antenna and UART communications
